# Fritzing sketch button (saved by Fritzing 0.9.9b)
breadboards: 1

parts:
  Raspberry_Pi_1 = Raspberry Pi 3 [part_number=RPI-3-V1.2]
  pull-up_circuit = Pushbutton [package="[THT]"]
  pull-down_circuit = Pushbutton [package="[THT]"]
  R2 = Resistor [tolerance=±5% power=0.25 resistance=1k package=THT]
  R3 = Resistor [tolerance=±5% power=0.25 resistance=1k package=THT]
  R4 = Resistor [tolerance=±5% power=0.25 resistance=10k package=THT]
  R1 = Resistor [tolerance=±5% power=0.25 resistance=10k package=THT]
  use_built-in_resistor_w/gpiozero = Pushbutton [package="[THT]"]

nets:
  N1: Raspberry_Pi_1.3v3, pull-down_circuit.Pin_3, pull-down_circuit.Pin_4, R4.Pin_1, use_built-in_resistor_w/gpiozero.Pin_3, use_built-in_resistor_w/gpiozero.Pin_4
  N2: Raspberry_Pi_1.GPIO2, use_built-in_resistor_w/gpiozero.Pin_1, use_built-in_resistor_w/gpiozero.Pin_2
  N3: Raspberry_Pi_1.GPIO9, R2.Pin_1
  N4: Raspberry_Pi_1.GPIO21, R3.Pin_1
  N5: Raspberry_Pi_1.GND, pull-up_circuit.Pin_3, pull-up_circuit.Pin_4, R1.Pin_1
  N6: pull-up_circuit.Pin_1, pull-up_circuit.Pin_2, R3.Pin_0, R4.Pin_0
  N7: pull-down_circuit.Pin_1, pull-down_circuit.Pin_2, R2.Pin_0, R1.Pin_0
